# Fritzing sketch LS7366R_double (saved by Fritzing 0.8.5b)
breadboards: 1

parts:
  Composants1 = Arduino Micro (Rev3)  # not connected
  LS7366R = IC, DIP package, 14 pins [chip_label=LS7366R part_number=LS7366R]
  LS7366R_2 = IC, DIP package, 14 pins [chip_label=LS7366R]
  S1 = Pushbutton [package="[THT]"]
  Encoder = female pin header, 5 pins [form="♀ (female)"]

nets:
  N1: LS7366R.pin2, LS7366R.pin3, LS7366R_2.pin2, S1.Pin_1, S1.Pin_2, Encoder.pin2
  N2: LS7366R.pin5, LS7366R_2.pin5
  N3: LS7366R.pin6, LS7366R_2.pin6
  N4: LS7366R.pin7, LS7366R_2.pin7
  N5: LS7366R.pin11, LS7366R_2.pin11, Encoder.pin4
  N6: LS7366R.pin12, LS7366R_2.pin12, Encoder.pin3
  N7: LS7366R.pin14, LS7366R_2.pin14, S1.Pin_3, S1.Pin_4, Encoder.pin1

notes:
  oscillator
  encoder
